// Logisim project cpu.circ as structural Verilog: 1 circuit, main circuit cpu
// ASel
module cpu (
  input  clk,
  input  [31:0] INSTRUCTION,
  input  [31:0] READ_DATA,
  output [31:0] WRITE_ADDRESS,
  output [31:0] PROGRAM_COUNTER,
  output [31:0] ra,
  output [31:0] sp,
  output [31:0] t0,
  output [31:0] t1,
  output [31:0] t2,
  output [31:0] s0,
  output [31:0] s1,
  output [31:0] a0,
  output [31:0] tohost,
  output [3:0] WRITE_ENABLE,
  output [31:0] WRITE_DATA
);

  wire ASel, BrEq, BrLt, Brun, BSel, CSRSel, CSRWen, MemRW, PCSel, RegWEn;
  wire [1:0] WBSel;
  wire [2:0] Immsel;
  wire [3:0] ALUSel;
  wire [4:0] AddrA, AddrB, AddrD;
  wire [31:0] adder_1_out, ALUInA, ALUInB, bit_extender_1_out, CSR_din, imm, INSTRUCTION_choose,
       INSTRUCTION_STATE, multiplexer_1_out, rs1, WB;

  Adder #(.width(32)) adder_1 (.a(PROGRAM_COUNTER), .b(32'h4), .out(adder_1_out));  // open: cin, cout
  Multiplexer #(.enable("false"), .width(32)) multiplexer_1 (
    .in0(adder_1_out), .in1(WRITE_ADDRESS), .out(multiplexer_1_out), .sel(PCSel));
  Register #(.width(32)) PC (.D(multiplexer_1_out), .clk(clk), .Q(PROGRAM_COUNTER));  // open: en, clr
  // Probe on {INSTRUCTION_choose[31:25], AddrB, AddrA, INSTRUCTION_choose[14:12], AddrD, INSTRUCTION_choose[6:0]}
  Multiplexer #(.enable("false"), .width(32)) multiplexer_2 (
    .in0(INSTRUCTION_STATE), .in1(32'h13),
    .out({INSTRUCTION_choose[31:25], AddrB, AddrA, INSTRUCTION_choose[14:12], AddrD, INSTRUCTION_choose[6:0]}),
    .sel(PCSel));
  // Probe on INSTRUCTION_STATE
  control_logic control_logic_1 (
    .CSRWen(CSRWen), .PCSel(PCSel), .RegWEn(RegWEn), .ImmSel(Immsel), .BrUn(Brun), .ASel(ASel), .BSel(BSel),
    .ALUSel(ALUSel), .MemRW(MemRW), .WBSel(WBSel), .CSRSel(CSRSel), .inst(INSTRUCTION_STATE), .BrEq(BrEq),
    .BrLt(BrLt));
  // Probe on INSTRUCTION
  Register #(.width(32)) irstD (.D(INSTRUCTION), .clk(clk), .Q(INSTRUCTION_STATE));  // open: en, clr
  // Probe on {INSTRUCTION_choose[31:25], AddrB, AddrA, INSTRUCTION_choose[14:12], AddrD, INSTRUCTION_choose[6:0]}
  // Probe on INSTRUCTION_STATE
  // Probe on AddrD
  // Probe on ALUSel
  // Probe on AddrD
  // Probe on WBSel
  // Probe on WB
  // Probe on Immsel
  regfile regfile_1 (
    .rs1(AddrA), .rs2(AddrB), .rd(AddrD), .Write_Data(WB), .RegWEn(RegWEn), .clk(clk), .ra(ra), .sp(sp),
    .t0(t0), .t1(t1), .t2(t2), .s0(s0), .s1(s1), .a0(a0), .Read_Data_1(rs1), .Read_Data_2(WRITE_DATA));
  // Probe on imm
  imm_gen imm_gen_1 (
    .inst({INSTRUCTION_choose[31:25], AddrB, AddrA, INSTRUCTION_choose[14:12], AddrD, INSTRUCTION_choose[6:0]}),
    .ImmSel(Immsel), .imm(imm));
  // Probe on PROGRAM_COUNTER
  // Probe on BSel
  Multiplexer #(.enable("false"), .width(32)) multiplexer_3 (
    .in0(rs1), .in1(PROGRAM_COUNTER), .out(ALUInA), .sel(ASel));
  Multiplexer #(.enable("false"), .width(32)) multiplexer_4 (.in0(WRITE_DATA), .in1(imm), .out(ALUInB), .sel(BSel));
  // Probe on ALUInB
  branch_comp branch_comp_1 (.rs1(rs1), .rs2(WRITE_DATA), .BrUn(Brun), .BrEq(BrEq), .BrLt(BrLt));
  assign bit_extender_1_out = {{27{1'b0}}, 5'b00001};  // Bit_Extender bit_extender_1
  // Probe on ALUInA
  // Probe on ALUSel
  Multiplexer #(.enable("false"), .width(32)) multiplexer_5 (
    .in0(t2), .in1(bit_extender_1_out), .out(CSR_din), .sel(CSRSel));
  alu alu_1 (.Result(WRITE_ADDRESS), .A(ALUInA), .B(ALUInB), .ALUSel(ALUSel));
  // Probe on WRITE_ADDRESS
  // Probe on WRITE_ENABLE
  assign WRITE_ENABLE = {{3{MemRW}}, MemRW};  // Bit_Extender bit_extender_2
  // Probe on WRITE_ADDRESS
  csr csr_1 (.CSR_address(12'h51e), .CSR_din(CSR_din), .CSR_WE(CSRWen), .clk(clk), .tohost(tohost));
  // Probe on WB
  Multiplexer #(.enable("false"), .select(2), .width(32)) multiplexer_6 (
    .in0(PROGRAM_COUNTER), .in1(WRITE_ADDRESS), .in2(READ_DATA), .out(WB), .sel(WBSel));  // open: in3

  // Other names for the same wires on the sheet: ALUOutput[31:0] = WRITE_ADDRESS;
  //   INSTRUCTION_choose (some bits) = {AddrB, AddrA, AddrD}; rs2[31:0] = WRITE_DATA

  // Notes on the sheet:
  //   Output to IMEM
  //   IMEM (do **NOT** move this)
  //   Inputs from IMEM
  //   Inputs/Outputs for testing. Do **NOT** move these.
  //   Outputs To DMEM
  //   DMEM (do **NOT** move this)
  //   Inputs From DMEM
endmodule
